# Fritzing sketch chesslr-mcp23017-boardlayout (saved by Fritzing 0.9.3b)
perfboards: 3
breadboards: 6

parts:
  IC1 = MCP23017 I2C I/O Expander  # not connected
  IC2 = MCP23017 I2C I/O Expander  # not connected
  IC3 = MCP23017 I2C I/O Expander  # not connected
  IC4 = MCP23017 I2C I/O Expander  # not connected
  IC5 = MCP23017 I2C I/O Expander  # not connected
  IC6 = MCP23017 I2C I/O Expander  # not connected
  IC7 = MCP23017 I2C I/O Expander  # not connected
  IC9 = MCP23017 I2C I/O Expander  # not connected
  J1 = male pin header, 4 pins [form="♂ (male)"]  # not connected
  J3 = female pin header, 16 pins [form="♀ (female)"]  # not connected
  J5 = female pin header, 16 pins [form="♀ (female)"]  # not connected
  J7 = female pin header, 16 pins [form="♀ (female)"]  # not connected
  J9 = female pin header, 16 pins [form="♀ (female)"]  # not connected
  J8 = female pin header, 16 pins [form="♀ (female)"]  # not connected
  J6 = female pin header, 16 pins [form="♀ (female)"]  # not connected
  J4 = female pin header, 16 pins [form="♀ (female)"]  # not connected
  J10 = female pin header, 16 pins [form="♀ (female)"]  # not connected
  J12 = female pin header, 8 pins [form="♀ (female)"]  # not connected
  IC10 = MCP23017 I2C I/O Expander  # not connected
  IC11 = MCP23017 I2C I/O Expander  # not connected
  IC12 = MCP23017 I2C I/O Expander  # not connected
  IC13 = MCP23017 I2C I/O Expander  # not connected
  J14 = male pin header, 6 pins [form="♂ (male)"]
  J15 = female pin header, 16 pins [form="♀ (female)"]  # not connected
  J16 = female pin header, 16 pins [form="♀ (female)"]
  J17 = female pin header, 16 pins [form="♀ (female)"]
  J18 = female pin header, 16 pins [form="♀ (female)"]  # not connected
  IC18 = MCP23017 I2C I/O Expander  # not connected
  IC19 = MCP23017 I2C I/O Expander  # not connected
  IC20 = MCP23017 I2C I/O Expander  # not connected
  IC21 = MCP23017 I2C I/O Expander  # not connected
  J19 = female pin header, 16 pins [form="♀ (female)"]  # not connected
  J21 = female pin header, 16 pins [form="♀ (female)"]  # not connected
  R1 = Resistor [tolerance=±5% resistance=10k package="1206 [SMD]"]
  R2 = Resistor [tolerance=±5% resistance=10k package="1206 [SMD]"]
  R3 = Resistor [tolerance=±5% resistance=10k package="1206 [SMD]"]
  R4 = Resistor [tolerance=±5% resistance=10k package="1206 [SMD]"]
  R5 = Resistor [tolerance=±5% resistance=10k package="1206 [SMD]"]
  R6 = Resistor [tolerance=±5% resistance=10k package="1206 [SMD]"]
  R7 = Resistor [tolerance=±5% resistance=10k package="1206 [SMD]"]
  R8 = Resistor [tolerance=±5% resistance=10k package="1206 [SMD]"]
  R9 = Resistor [tolerance=±5% resistance=10k package="1206 [SMD]"]
  R10 = Resistor [tolerance=±5% resistance=10k package="1206 [SMD]"]
  R11 = Resistor [tolerance=±5% resistance=10k package="1206 [SMD]"]
  R12 = Resistor [tolerance=±5% resistance=10k package="1206 [SMD]"]
  R13 = Resistor [tolerance=±5% resistance=10k package="1206 [SMD]"]
  R14 = Resistor [tolerance=±5% resistance=10k package="1206 [SMD]"]
  R18 = Resistor [tolerance=±5% resistance=10k package="0805 [SMD]"]
  R19 = Resistor [tolerance=±5% resistance=10k package="0805 [SMD]"]
  R21 = Resistor [tolerance=±5% resistance=10k package="0805 [SMD]"]
  R22 = Resistor [tolerance=±5% resistance=10k package="0805 [SMD]"]
  R23 = Resistor [tolerance=±5% resistance=10k package="0805 [SMD]"]
  R24 = Resistor [tolerance=±5% resistance=10k package="0805 [SMD]"]
  R25 = Resistor [tolerance=±5% resistance=10k package="0805 [SMD]"]
  R26 = Resistor [tolerance=±5% resistance=10k package="0805 [SMD]"]
  R27 = Resistor [tolerance=±5% resistance=10k package="0805 [SMD]"]
  R28 = Resistor [tolerance=±5% resistance=10k package="0805 [SMD]"]
  R29 = Resistor [tolerance=±5% resistance=10k package="0805 [SMD]"]
  R30 = Resistor [tolerance=±5% resistance=10k package="0805 [SMD]"]
  R31 = Resistor [tolerance=±5% resistance=10k package="0805 [SMD]"]
  R32 = Resistor [tolerance=±5% resistance=10k package="0805 [SMD]"]
  R33 = Resistor [tolerance=±5% resistance=10k package="0805 [SMD]"]
  R34 = Resistor [tolerance=±5% resistance=10k package="0805 [SMD]"]
  R35 = Resistor [tolerance=±5% resistance=10k package="0805 [SMD]"]
  R36 = Resistor [tolerance=±5% resistance=10k package="0805 [SMD]"]
  J22 = female pin header, 16 pins [form="♀ (female)"]
  J23 = female pin header, 16 pins [form="♀ (female)"]
  R37 = Resistor [tolerance=±5% resistance=10k package="1206 [SMD]"]
  R38 = Resistor [tolerance=±5% resistance=10k package="1206 [SMD]"]
  R39 = Resistor [tolerance=±5% resistance=10k package="1206 [SMD]"]
  R40 = Resistor [tolerance=±5% resistance=10k package="1206 [SMD]"]
  R41 = Resistor [tolerance=±5% resistance=10k package="1206 [SMD]"]
  R42 = Resistor [tolerance=±5% resistance=10k package="1206 [SMD]"]
  R43 = Resistor [tolerance=±5% resistance=10k package="1206 [SMD]"]
  R44 = Resistor [tolerance=±5% resistance=10k package="1206 [SMD]"]
  R45 = Resistor [tolerance=±5% resistance=10k package="1206 [SMD]"]
  R46 = Resistor [tolerance=±5% resistance=10k package="1206 [SMD]"]
  R47 = Resistor [tolerance=±5% resistance=10k package="1206 [SMD]"]
  R48 = Resistor [tolerance=±5% resistance=10k package="1206 [SMD]"]
  R49 = Resistor [tolerance=±5% resistance=10k package="1206 [SMD]"]
  R50 = Resistor [tolerance=±5% resistance=10k package="1206 [SMD]"]
  R51 = Resistor [tolerance=±5% resistance=10k package="0805 [SMD]"]
  R52 = Resistor [tolerance=±5% resistance=10k package="0805 [SMD]"]
  R53 = Resistor [tolerance=±5% resistance=10k package="0805 [SMD]"]
  R54 = Resistor [tolerance=±5% resistance=10k package="0805 [SMD]"]
  R55 = Resistor [tolerance=±5% resistance=10k package="0805 [SMD]"]
  R56 = Resistor [tolerance=±5% resistance=10k package="0805 [SMD]"]
  R57 = Resistor [tolerance=±5% resistance=10k package="0805 [SMD]"]
  R58 = Resistor [tolerance=±5% resistance=10k package="0805 [SMD]"]
  R59 = Resistor [tolerance=±5% resistance=10k package="0805 [SMD]"]
  R60 = Resistor [tolerance=±5% resistance=10k package="0805 [SMD]"]
  R61 = Resistor [tolerance=±5% resistance=10k package="0805 [SMD]"]
  R62 = Resistor [tolerance=±5% resistance=10k package="0805 [SMD]"]
  R63 = Resistor [tolerance=±5% resistance=10k package="0805 [SMD]"]
  R64 = Resistor [tolerance=±5% resistance=10k package="0805 [SMD]"]
  R65 = Resistor [tolerance=±5% resistance=10k package="0805 [SMD]"]
  R66 = Resistor [tolerance=±5% resistance=10k package="0805 [SMD]"]
  R67 = Resistor [tolerance=±5% resistance=10k package="0805 [SMD]"]
  R68 = Resistor [tolerance=±5% resistance=10k package="0805 [SMD]"]
  R69 = Resistor [tolerance=±5% resistance=220 package="2010 [SMD]"]
  IC22 = MCP23017 I2C I/O Expander
  R70 = Resistor [tolerance=±5% resistance=220 package="2010 [SMD]"]
  R71 = Resistor [tolerance=±5% resistance=220 package="2010 [SMD]"]
  R72 = Resistor [tolerance=±5% resistance=220 package="2010 [SMD]"]
  R73 = Resistor [tolerance=±5% resistance=220 package="2010 [SMD]"]
  R74 = Resistor [tolerance=±5% resistance=10k package="1206 [SMD]"]
  R75 = Resistor [tolerance=±5% resistance=10k package="1206 [SMD]"]
  R76 = Resistor [tolerance=±5% resistance=10k package="1206 [SMD]"]
  R77 = Resistor [tolerance=±5% resistance=10k package="1206 [SMD]"]
  R78 = Resistor [tolerance=±5% resistance=10k package="1206 [SMD]"]
  R79 = Resistor [tolerance=±5% resistance=220 package="2010 [SMD]"]
  R80 = Resistor [tolerance=±5% resistance=220 package="2010 [SMD]"]
  R81 = Resistor [tolerance=±5% resistance=220 package="2010 [SMD]"]
  R82 = Resistor [tolerance=±5% resistance=10k package="1206 [SMD]"]
  R83 = Resistor [tolerance=±5% resistance=10k package="1206 [SMD]"]
  R84 = Resistor [tolerance=±5% resistance=10k package="1206 [SMD]"]
  J24 = female pin header, 16 pins [form="♀ (female)"]  # not connected
  J25 = female pin header, 16 pins [form="♀ (female)"]  # not connected
  J26 = female pin header, 16 pins [form="♀ (female)"]  # not connected
  R85 = Resistor [tolerance=±5% resistance=10k package="1206 [SMD]"]  # not connected
  R86 = Resistor [tolerance=±5% resistance=10k package="1206 [SMD]"]  # not connected
  R87 = Resistor [tolerance=±5% resistance=10k package="1206 [SMD]"]  # not connected
  R88 = Resistor [tolerance=±5% resistance=10k package="1206 [SMD]"]  # not connected
  R89 = Resistor [tolerance=±5% resistance=10k package="1206 [SMD]"]  # not connected
  R90 = Resistor [tolerance=±5% resistance=10k package="1206 [SMD]"]  # not connected
  R91 = Resistor [tolerance=±5% resistance=10k package="1206 [SMD]"]  # not connected
  R92 = Resistor [tolerance=±5% resistance=10k package="1206 [SMD]"]  # not connected
  R93 = Resistor [tolerance=±5% resistance=220 package="2010 [SMD]"]  # not connected
  R94 = Resistor [tolerance=±5% resistance=220 package="2010 [SMD]"]  # not connected
  R95 = Resistor [tolerance=±5% resistance=220 package="2010 [SMD]"]  # not connected
  R96 = Resistor [tolerance=±5% resistance=220 package="2010 [SMD]"]  # not connected
  R97 = Resistor [tolerance=±5% resistance=220 package="2010 [SMD]"]  # not connected
  R98 = Resistor [tolerance=±5% resistance=220 package="2010 [SMD]"]  # not connected
  R99 = Resistor [tolerance=±5% resistance=220 package="2010 [SMD]"]  # not connected
  R100 = Resistor [tolerance=±5% resistance=220 package="2010 [SMD]"]  # not connected
  IC23 = MCP23017 I2C I/O Expander  # not connected
  R101 = Resistor [tolerance=±5% resistance=220 package="0603 [SMD]"]  # not connected
  IC24 = MCP23017 I2C I/O Expander  # not connected
  R102 = Resistor [tolerance=±5% resistance=10k package="0603 [SMD]"]  # not connected
  IC25 = MCP23017 I2C I/O Expander  # not connected
  R103 = Resistor [tolerance=±5% resistance=220 package="0603 [SMD]"]  # not connected
  R104 = Resistor [tolerance=±5% resistance=10k package="0603 [SMD]"]  # not connected
  R105 = Resistor [tolerance=±5% resistance=10k package="0603 [SMD]"]  # not connected
  U1 = AVR 10-pin ICSP Header [package=2x5-shrouded_smd]  # not connected
  JP1 = Header 5x2 [package=avr_icsp]  # not connected

nets:
  N1: J14.pin6, R1.Pin_1, R2.Pin_1, R3.Pin_1, R4.Pin_1, R5.Pin_1, R6.Pin_1, R7.Pin_1, R8.Pin_1, R9.Pin_1, R10.Pin_1, R11.Pin_1, R12.Pin_1, R13.Pin_1, R14.Pin_1, R18.Pin_1, R19.Pin_1, R21.Pin_1, R22.Pin_1, R23.Pin_1, R24.Pin_1, R25.Pin_1, R26.Pin_1, R27.Pin_1, R28.Pin_1, R30.Pin_1, R31.Pin_1, R32.Pin_1, R33.Pin_1, R34.Pin_1, R35.Pin_1, R36.Pin_1
  N2: J16.pin1, R1.Pin_0
  N3: J16.pin2, R2.Pin_0
  N4: J16.pin3, R3.Pin_0
  N5: J16.pin4, R4.Pin_0
  N6: J16.pin5, R5.Pin_0
  N7: J16.pin6, R6.Pin_0
  N8: J16.pin7, R7.Pin_0
  N9: J16.pin8, R8.Pin_0
  N10: J16.pin9, R9.Pin_0
  N11: J16.pin10, R10.Pin_0
  N12: J16.pin11, R11.Pin_0
  N13: J16.pin12, R12.Pin_0
  N14: J16.pin13, R13.Pin_0
  N15: J16.pin14, R14.Pin_0
  N16: J16.pin15, R34.Pin_0
  N17: J16.pin16, R35.Pin_0
  N18: J17.pin1, R18.Pin_0
  N19: J17.pin2, R19.Pin_0
  N20: J17.pin3, R36.Pin_0
  N21: J17.pin4, R21.Pin_0
  N22: J17.pin5, R22.Pin_0
  N23: J17.pin6, R23.Pin_0
  N24: J17.pin7, R24.Pin_0
  N25: J17.pin8, R25.Pin_0
  N26: J17.pin9, R29.Pin_0
  N27: J17.pin10, R26.Pin_0
  N28: J17.pin11, R27.Pin_0
  N29: J17.pin12, R28.Pin_0
  N30: J17.pin13, R30.Pin_0
  N31: J17.pin14, R31.Pin_0
  N32: J17.pin15, R32.Pin_0
  N33: J17.pin16, R33.Pin_0
  N34: J22.pin1, R62.Pin_0
  N35: J22.pin2, R59.Pin_0
  N36: J22.pin3, R60.Pin_0
  N37: J22.pin4, R56.Pin_0
  N38: J22.pin5, R63.Pin_0
  N39: J22.pin6, R53.Pin_0
  N40: J22.pin7, R68.Pin_0
  N41: J22.pin8, R66.Pin_0
  N42: J22.pin9, R61.Pin_0
  N43: J22.pin10, R55.Pin_0
  N44: J22.pin11, R51.Pin_0
  N45: J22.pin12, R57.Pin_0
  N46: J22.pin13, R65.Pin_0
  N47: J22.pin14, R58.Pin_0
  N48: J22.pin15, R64.Pin_0
  N49: J22.pin16, R54.Pin_0
  N50: J23.pin1, R47.Pin_0
  N51: J23.pin2, R39.Pin_0
  N52: J23.pin3, R46.Pin_0
  N53: J23.pin4, R50.Pin_0
  N54: J23.pin5, R41.Pin_0
  N55: J23.pin6, R37.Pin_0
  N56: J23.pin7, R42.Pin_0
  N57: J23.pin8, R40.Pin_0
  N58: J23.pin9, R44.Pin_0
  N59: J23.pin10, R38.Pin_0
  N60: J23.pin11, R45.Pin_0
  N61: J23.pin12, R43.Pin_0
  N62: J23.pin13, R49.Pin_0
  N63: J23.pin14, R48.Pin_0
  N64: J23.pin15, R67.Pin_0
  N65: J23.pin16, R52.Pin_0
  N66: R37.Pin_1, R38.Pin_1, R39.Pin_1, R40.Pin_1, R41.Pin_1, R42.Pin_1, R43.Pin_1, R44.Pin_1, R45.Pin_1, R46.Pin_1, R47.Pin_1, R48.Pin_1, R49.Pin_1, R50.Pin_1, R51.Pin_1, R52.Pin_1, R53.Pin_1, R54.Pin_1, R55.Pin_1, R56.Pin_1, R57.Pin_1, R58.Pin_1, R59.Pin_1, R60.Pin_1, R62.Pin_1, R63.Pin_1, R64.Pin_1, R65.Pin_1, R66.Pin_1, R67.Pin_1, R68.Pin_1
  N67: R69.Pin_0, IC22.GPA6
  N68: IC22.GPB0, R74.Pin_1
  N69: IC22.GPB1, R75.Pin_1
  N70: IC22.GPB2, R76.Pin_1
  N71: IC22.GPB3, R77.Pin_1
  N72: IC22.GPB4, R78.Pin_1
  N73: IC22.GPB5, R82.Pin_1
  N74: IC22.GPB6, R83.Pin_1
  N75: IC22.GPB7, R84.Pin_1
  N76: IC22.GPA0, R81.Pin_0
  N77: IC22.GPA1, R80.Pin_0
  N78: IC22.GPA2, R79.Pin_0
  N79: IC22.GPA3, R73.Pin_0
  N80: IC22.GPA4, R71.Pin_0
  N81: IC22.GPA5, R70.Pin_0
  N82: IC22.GPA7, R72.Pin_0

notes:
  8 female pins are for a negative pin for each row.
  May just use 1 neg pin for all rows.
  4 Pins at top are male and used for power and i2c.
  Red Vdd Blk Vss
  White SCL Yello SDA
  Each row of the board connects to one chip:
  8 on left for Reed switches.
  8 on right for LED.
  Chip order:
  1 (0x20) 2 (0x21) 3 (0x22) 4 (0x23)
  5 (0x24) 6 (0x25) 7 (0x26) 8 (0x27)
  Note that there are 4 pins that are not connected for each chip.
  MCP Perf board
  Size: 30x24
  Used for connecting chess board LED and Reed switches.
  Resistors use 5 holes

custom parts:
  MCP23017 I2C I/O Expander: The MCP23017 uses two i2c pins (these can be shared with other i2c devices), and in exchange gives you 16 general purpose pins. You can set each of 16 pins to be input, output, input with a pullup or open drain. There's even the ability to get an interrupt via an external pin when any of the inputs change so you don't have to keep polling the chip.
