# Fritzing sketch mcp-3x3 (saved by Fritzing 0.9.3b)

parts:
  IC1_-_LED = MCP23017 I2C I/O Expander
  R10 = Resistor [tolerance=±5% resistance=220 package="0603 [SMD]"]
  R11 = Resistor [tolerance=±5% resistance=220 package="0603 [SMD]"]
  R12 = Resistor [tolerance=±5% resistance=220 package="0603 [SMD]"]
  R13 = Resistor [tolerance=±5% resistance=220 package="0603 [SMD]"]
  R14 = Resistor [tolerance=±5% resistance=220 package="0603 [SMD]"]
  R15 = Resistor [tolerance=±5% resistance=220 package="0603 [SMD]"]
  R16 = Resistor [tolerance=±5% resistance=220 package="0603 [SMD]"]
  R17 = Resistor [tolerance=±5% resistance=220 package="0603 [SMD]"]
  R18 = Resistor [tolerance=±5% resistance=220 package="0603 [SMD]"]
  Level_shifter = Adafruit 4-channel I2C-safe Bi-directional Logic Level Converter [part_number="Adafruit #757"]
  J1 = female pin header, 6 pins [form="♀ (female)"]
  J2 = female pin header, 19 pins [form="♀ (female)"]
  J3 = female pin header, 2 pins [form="♀ (female)"]
  R19 = Resistor [tolerance=±5% resistance=10k package="0603 [SMD]"]
  R20 = Resistor [tolerance=±5% resistance=10k package="0603 [SMD]"]
  R21 = Resistor [tolerance=±5% resistance=10k package="0603 [SMD]"]
  R22 = Resistor [tolerance=±5% resistance=10k package="0603 [SMD]"]
  R23 = Resistor [tolerance=±5% resistance=10k package="0603 [SMD]"]
  R24 = Resistor [tolerance=±5% resistance=10k package="0603 [SMD]"]
  R25 = Resistor [tolerance=±5% resistance=10k package="0603 [SMD]"]
  R26 = Resistor [tolerance=±5% resistance=10k package="0603 [SMD]"]
  R27 = Resistor [tolerance=±5% resistance=10k package="0603 [SMD]"]
  IC2_-_Reed = MCP23017 I2C I/O Expander
  LED1 = LED - 5mm [color="Red (633nm)" package="5 mm [THT]"]
  LED2 = LED - 5mm [color="Red (633nm)" package="5 mm [THT]"]
  LED3 = LED - 5mm [color="Red (633nm)" package="5 mm [THT]"]
  LED4 = LED - 5mm [color="Red (633nm)" package="5 mm [THT]"]
  LED5 = LED - 5mm [color="Red (633nm)" package="5 mm [THT]"]
  LED6 = LED - 5mm [color="Red (633nm)" package="5 mm [THT]"]
  LED7 = LED - 5mm [color="Red (633nm)" package="5 mm [THT]"]
  LED8 = LED - 5mm [color="Red (633nm)" package="5 mm [THT]"]
  LED9 = LED - 5mm [color="Red (633nm)" package="5 mm [THT]"]
  S1 = Reed switch [package=THT]
  S2 = Reed switch [package=THT]
  S3 = Reed switch [package=THT]
  S4 = Reed switch [package=THT]
  S5 = Reed switch [package=THT]
  S6 = Reed switch [package=THT]
  S7 = Reed switch [package=THT]
  S8 = Reed switch [package=THT]
  S9 = Reed switch [package=THT]
  R28 = Resistor [tolerance=±5% resistance=4.7k package="0603 [SMD]"]
  R29 = Resistor [tolerance=±5% resistance=4.7k package="0603 [SMD]"]

nets:
  N1: IC1_-_LED.GPB0, R12.Pin_1
  5V: IC1_-_LED.VDD, IC1_-_LED.RESET, Level_shifter.HV, J3.pin1, R19.Pin_0, R20.Pin_0, R21.Pin_0, R22.Pin_0, R23.Pin_0, R24.Pin_0, R25.Pin_0, R26.Pin_0, R27.Pin_0, IC2_-_Reed.VDD, IC2_-_Reed.A0, IC2_-_Reed.RESET, R28.Pin_1, R29.Pin_1
  GND: IC1_-_LED.VSS, IC1_-_LED.A0, IC1_-_LED.A1, IC1_-_LED.A2, Level_shifter.GND, J1.pin1, J2.pin1, J3.pin2, IC2_-_Reed.VSS, IC2_-_Reed.A1, IC2_-_Reed.A2, LED1.cathode, LED2.cathode, LED3.cathode, LED4.cathode, LED5.cathode, LED6.cathode, LED7.cathode, LED8.cathode, LED9.cathode, S1.pin_1, S2.pin_1, S3.pin_1, S4.pin_1, S5.pin_1, S6.pin_1, S7.pin_1, S8.pin_1, S9.pin_1
  N2: IC1_-_LED.SCL, Level_shifter.B1, IC2_-_Reed.SCL, R29.Pin_0
  N3: IC1_-_LED.SDA, Level_shifter.B2, IC2_-_Reed.SDA, R28.Pin_0
  N4: IC1_-_LED.GPA0, R17.Pin_1
  N5: IC1_-_LED.GPA1, R13.Pin_1
  N6: IC1_-_LED.GPA2, R14.Pin_1
  N7: IC1_-_LED.GPA3, R11.Pin_1
  N8: IC1_-_LED.GPA4, R15.Pin_1
  N9: IC1_-_LED.GPA5, R10.Pin_1
  N10: IC1_-_LED.GPA6, R18.Pin_1
  N11: IC1_-_LED.GPA7, R16.Pin_1
  N12: R10.Pin_0, J2.pin7, LED6.anode
  N13: R11.Pin_0, J2.pin5, LED4.anode
  N14: R12.Pin_0, J2.pin10, LED9.anode
  N15: R13.Pin_0, J2.pin3, LED2.anode
  N16: R14.Pin_0, J2.pin4, LED3.anode
  N17: R15.Pin_0, J2.pin6, LED5.anode
  N18: R16.Pin_0, J2.pin9, LED8.anode
  N19: R17.Pin_0, J2.pin2, LED1.anode
  N20: R18.Pin_0, J2.pin8, LED7.anode
  N21: Level_shifter.A2, J1.pin4
  N22: Level_shifter.A1, J1.pin5
  N23: Level_shifter.LV, J1.pin3
  N24: J2.pin11, R19.Pin_1, IC2_-_Reed.GPA0, S1.pin_2
  N25: J2.pin12, R20.Pin_1, IC2_-_Reed.GPA1, S2.pin_2
  N26: J2.pin13, R21.Pin_1, IC2_-_Reed.GPA2, S3.pin_2
  N27: J2.pin14, R22.Pin_1, IC2_-_Reed.GPA3, S4.pin_2
  N28: J2.pin15, R23.Pin_1, IC2_-_Reed.GPA4, S5.pin_2
  N29: J2.pin16, R24.Pin_1, IC2_-_Reed.GPA5, S6.pin_2
  N30: J2.pin17, R25.Pin_1, IC2_-_Reed.GPA6, S7.pin_2
  N31: J2.pin18, R26.Pin_1, IC2_-_Reed.GPA7, S8.pin_2
  N32: J2.pin19, R27.Pin_1, IC2_-_Reed.GPB0, S9.pin_2

notes:
  R19-27 are pull-up resistors. Not using the internal pull-ups on the 23017 as the chip went bad during testing.
  Level shifter required because MCP's are running at 5V and RPi requires 3.3V signals.
  NOTE:
  You may need 2 4.7K resistors from SDL to 5V and SDA to 5V.
  MCP interface board
  Final Draft
  Board that connects the 3x3 chess board with LEDs and Reed switches to the RPi. Communication is through i2c. You can run the curcuit at 5V, but RPi uses the level shifter to talk with the rest of it as it runs at 3.3V.
  i2c address 0x21
  i2c address 0x20
  Left Input 0x21
  Right LED 0x20

custom parts:
  MCP23017 I2C I/O Expander: The MCP23017 uses two i2c pins (these can be shared with other i2c devices), and in exchange gives you 16 general purpose pins. You can set each of 16 pins to be input, output, input with a pullup or open drain. There's even the ability to get an interrupt via an external pin when any of the inputs change so you don't have to keep polling the chip.
  Adafruit 4-channel I2C-safe Bi-directional Logic Level Converter: Because the Arduino (and Basic Stamp) are 5V devices, and most modern sensors, displays, flash cards and modes are 3.3V-only, many makers find that they need to perform level shifting/conversion to protect the 3.3V device from 5V. We do have some other handy level shifters in the shop, from the DIP 74LVC245 to the fancy bi-directional TXB0108. However, neither of these are happy to work with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
