# Fritzing sketch multipower (saved by Fritzing 0.9.3b)
breadboards: 1

parts:
  RPi1 = Adafruit Pi T-Cobbler [part_number="Adafruit #1754 and #1105"]
  3_3V = 4 x AAA Battery Mount
  MCP23017_(0x20)1 = ZIFSOCKET-28-3 [package=dil28-3-zif_socket]
  LED2 = LED - 3mm [color="Blue (525nm)" package="3 mm [THT]"]
  R8 = Resistor [tolerance=±5% resistance=330 package="1206 [SMD]"]

nets (from the schematic view):
  N1: RPi1.SDA, MCP23017_(0x20)1.P$13
  N2: RPi1.GND, 3_3V.-, MCP23017_(0x20)1.P$10, MCP23017_(0x20)1.P$15, MCP23017_(0x20)1.P$16, MCP23017_(0x20)1.P$17, R8.Pin_1
  N3: RPi1.SCL, MCP23017_(0x20)1.P$12
  N4: 3_3V.+, MCP23017_(0x20)1.P$9
  N5: MCP23017_(0x20)1.P$21, LED2.anode
  N6: LED2.cathode, R8.Pin_0

custom parts:
  Adafruit Pi T-Cobbler: Now that you've finally got your hands on a Raspberry Pi® , you're probably itching to make some fun embedded computer projects with it. What you need is an assembled add on prototyping Pi T-Cobbler from Adafruit, which can break out all those tasty power, GPIO, I2C and SPI pins from the 26 pin header onto a solderless breadboard. This mini kit will make "cobbling together" prototypes with the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
