# Fritzing sketch proto01 (saved by Fritzing 0.9.3b)
breadboards: 1

parts:
  MCP23017_(0x20) = ZIFSOCKET-28-3 [package=dil28-3-zif_socket]
  S1 = Momentary Switch [package=ksa_sealed_tac_switch]
  R1 = Resistor [tolerance=±5% resistance=10k package="1206 [SMD]"]
  RPi = Adafruit Pi T-Cobbler [part_number="Adafruit #1754 and #1105"]
  R2 = Resistor [tolerance=±5% resistance=4.7k package="1206 [SMD]"]
  R3 = Resistor [tolerance=±5% resistance=4.7k package="1206 [SMD]"]
  LED2 = LED - 3mm [color="Blue (525nm)" package="3 mm [THT]"]
  MCP23017_(0x21) = ZIFSOCKET-28-3 [package=dil28-3-zif_socket]
  R4 = Resistor [tolerance=±5% resistance=330 package="1206 [SMD]"]
  R7 = Resistor [tolerance=±5% resistance=330 package="1206 [SMD]"]
  R8 = Resistor [tolerance=±5% resistance=330 package="1206 [SMD]"]
  LED3 = LED - 3mm [color="Blue (525nm)" package="3 mm [THT]"]
  LED1 = LED - 3mm [color="Blue (525nm)" package="3 mm [THT]"]

nets:
  N1: MCP23017_(0x20).P$1, S1.3
  N2: MCP23017_(0x20).P$8, LED2.anode
  N3: MCP23017_(0x20).P$9, MCP23017_(0x20).P$18, RPi.3.3V, R2.Pin_0, R3.Pin_0, MCP23017_(0x21).P$9, MCP23017_(0x21).P$15, MCP23017_(0x21).P$18
  GND: MCP23017_(0x20).P$10, MCP23017_(0x20).P$15, MCP23017_(0x20).P$16, MCP23017_(0x20).P$17, R1.Pin_0, RPi.GND, MCP23017_(0x21).P$10, MCP23017_(0x21).P$16, MCP23017_(0x21).P$17, R4.Pin_1, R7.Pin_1, R8.Pin_0
  N4: MCP23017_(0x20).P$12, RPi.SCL, R3.Pin_1, MCP23017_(0x21).P$12
  N5: MCP23017_(0x20).P$13, RPi.SDA, R2.Pin_1, MCP23017_(0x21).P$13
  N6: MCP23017_(0x20).P$21, LED1.anode
  N7: S1.1, R1.Pin_1
  N8: LED2.cathode, R8.Pin_1
  N9: MCP23017_(0x21).P$22, LED3.anode
  N10: R4.Pin_0, LED3.cathode
  N11: R7.Pin_0, LED1.cathode

custom parts:
  Adafruit Pi T-Cobbler: Now that you've finally got your hands on a Raspberry Pi® , you're probably itching to make some fun embedded computer projects with it. What you need is an assembled add on prototyping Pi T-Cobbler from Adafruit, which can break out all those tasty power, GPIO, I2C and SPI pins from the 26 pin header onto a solderless breadboard. This mini kit will make "cobbling together" prototypes with the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
